# Fritzing sketch wiring (saved by Fritzing 0.9.2b)
circuit board: 6.06394cm x 5.13539cm
breadboards: 1

parts:
  U1 = 74HC595 [package="DIP16 [THT]"]
  R1 = Resistor [tolerance=±5% resistance=470 package=THT]
  R5 = Resistor [tolerance=±5% resistance=470 package=THT]
  R2 = Resistor [tolerance=±5% resistance=470 package=THT]
  R6 = Resistor [tolerance=±5% resistance=470 package=THT]
  R7 = Resistor [tolerance=±5% resistance=470 package=THT]
  R4 = Resistor [tolerance=±5% resistance=470 package=THT]
  R8 = Resistor [tolerance=±5% resistance=470 package=THT]
  LED1 = LED - 3mm [color="White (4500K)" package="3 mm [THT]"]
  LED2 = LED - 3mm [color="White (4500K)" package="3 mm [THT]"]
  LED3 = LED - 3mm [color="White (4500K)" package="3 mm [THT]"]
  LED4 = LED - 3mm [color="White (4500K)" package="3 mm [THT]"]
  LED5 = LED - 3mm [color="White (4500K)" package="3 mm [THT]"]
  LED6 = LED - 3mm [color="White (4500K)" package="3 mm [THT]"]
  LED7 = LED - 3mm [color="White (4500K)" package="3 mm [THT]"]
  LED8 = LED - 3mm [color="White (4500K)" package="3 mm [THT]"]
  R3 = Resistor [tolerance=±5% resistance=470 package=THT]
  Raspberry_Pi2 = Raspberry Pi 2

nets:
  N1: U1.Q1, R2.Pin_0
  N2: U1.Q2, R3.Pin_0
  N3: U1.Q3, R4.Pin_0
  N4: U1.Q4, R5.Pin_0
  N5: U1.Q5, R6.Pin_0
  N6: U1.Q6, R7.Pin_0
  N7: U1.Q7, R8.Pin_0
  GND: U1.GND, U1.OE, LED1.anode, LED2.anode, LED3.anode, LED4.anode, LED5.anode, LED6.anode, LED7.anode, LED8.anode, Raspberry_Pi2.GND
  VCC: U1.MR, U1.VCC, Raspberry_Pi2.5V
  N8: U1.SH_CP, Raspberry_Pi2.GIPO22
  N9: U1.ST_CP, Raspberry_Pi2.GIPO23
  N10: U1.DS, Raspberry_Pi2.GIPO27
  N11: U1.Q0, R1.Pin_0
  N12: R1.Pin_1, LED1.cathode
  N13: R5.Pin_1, LED5.cathode
  N14: R2.Pin_1, LED2.cathode
  N15: R6.Pin_1, LED6.cathode
  N16: R7.Pin_1, LED7.cathode
  N17: R4.Pin_1, LED4.cathode
  N18: R8.Pin_1, LED8.cathode
  N19: LED3.cathode, R3.Pin_1
